# Fritzing sketch Hangman (saved by Fritzing 0.8.7b)
breadboards: 1

parts:
  LCD1 = LCD screen
  Part1 = Arduino Uno (Rev3)
  R1 = Trimmer Potentiometer [maximum_resistance=10kΩ package=THT]
  Part2 = Breadboard Power Supply Board SMD
  Part3 = Thumb Joystick
  SG1 = Buzzer 12mm [package=buzzer-12mm-ns]
  X1 = X113647 Stepper Driver Board [package=board]
  MOTOR1 = Adafruit Gear-Reduced Stepper Motor (small)

nets:
  GND: LCD1.VSS, LCD1.R/W, LCD1.LED-, Part1.GND, R1.leg2, Part2.GND, Part3.GND, SG1.2, X1.GND
  VCC: LCD1.VDD, Part1.5V, R1.leg1, Part2.VCC, Part3.VCC, X1.+V
  N1: LCD1.V0, R1.wiper
  N2: LCD1.RS, Part1.D7
  N3: LCD1.E, Part1.D8
  N4: LCD1.DB4, Part1.D13/SCK
  N5: LCD1.DB5, Part1.D10_PWM/SS
  N6: LCD1.DB6, Part1.D11_PWM/MOSI
  N7: LCD1.DB7, Part1.D12/MISO
  N8: Part1.A0, Part3.VERT
  N9: Part1.A1, Part3.HORZ
  N10: Part1.D9_PWM, SG1.1
  N11: Part1.D2, X1.IN1
  N12: Part1.D3_PWM, X1.IN2
  N13: Part1.D4, X1.IN3
  N14: Part1.D5_PWM, X1.IN4
  N15: X1.BLUE, MOTOR1.RED
  N16: X1.PINK, MOTOR1.ORANGE
  N17: X1.YELLOW, MOTOR1.YELLOW
  N18: X1.ORANGE, MOTOR1.PINK
  N19: X1.RED, MOTOR1.BLUE

custom parts:
  X113647 Stepper Driver Board: A common stepper motor driver board based on ULN2003APG darlington array
  Adafruit Gear-Reduced Stepper Motor (small): Adafruit gear-reduction stepper motor (small)
